# Fritzing sketch conexión i2c raspberry pi arduino (saved by Fritzing 0.8.3b)
breadboards: 1

parts:
  Parte1 = Arduino Uno (Rev3)
  Raspberry_Pi_rev1 = Raspberry Pi rev1
  Parte2 = Logic Level Converter
  LED1 = LED - 3mm [color="Red (633nm)" package="3 mm [THT]"]
  S1 = Pushbutton [package="[THT]"]
  R1 = Resistor [tolerance=±5% resistance=220 package=THT]

nets:
  N1: Parte1.A4/SDA, Parte2.TX2_LV
  N2: Parte1.A5/SCL, Parte2.TX_LV
  GND: Parte1.GND, Raspberry_Pi_rev1.GND, Parte2.GND, LED1.anode, R1.Pin_1
  N3: Parte1.D13/SCK, LED1.cathode
  N4: Parte1.5V, Parte2.LV
  N5: Raspberry_Pi_rev1.3V3, Parte2.HV, S1.Pin_3, S1.Pin_4
  N6: Raspberry_Pi_rev1.GIPO_0, Parte2.TX2_HV
  N7: Raspberry_Pi_rev1.GIPO_1, Parte2.TX_HV
  N8: Raspberry_Pi_rev1.GPIO_17, S1.Pin_1, S1.Pin_2
